// Logisim project ALU.circ as structural Verilog: 1 circuit, main circuit ALU
module ALU (
  input  [7:0] Input_Data,
  input  Operation,
  input  [7:0] in_3,
  input  IR_Load,
  output [7:0] Result
);

  wire clock_1_out;
  wire [7:0] Instruction_Register_q;

  Clock clock_1 (.out(clock_1_out));
  Register Instruction_Register (.D(in_3), .en(IR_Load), .Q(Instruction_Register_q), .clk(clock_1_out));  // open: clr
  Multiplexer #(.width(8)) multiplexer_1 (
    .in0({Input_Data[6:0], Input_Data[7]}), .in1({Input_Data[0], Input_Data[7:1]}), .out(Result),
    .sel(Operation));  // open: en
endmodule
