// Logisim project MPFinal.circ as structural Verilog: 3 circuits, main circuit main
module ALU (
  input  [7:0] Input_Data,
  input  Operation,
  output [7:0] Result
);

  Multiplexer #(.width(8)) multiplexer_1 (
    .in0({Input_Data[6:0], Input_Data[7]}), .in1({Input_Data[0], Input_Data[7:1]}), .out(Result),
    .sel(Operation));  // open: en
endmodule

module Decoder (
  input  [7:0] Opcode,
  output Reg_Select,
  output ALU_Op,
  output Write_Enable,
  output [1:0] Bus_Select
);

  wire comparator_1_eq, comparator_2_eq, comparator_3_eq, comparator_4_eq;

  Comparator comparator_1 (.a(Opcode), .b(8'h1), .eq(comparator_1_eq));  // open: gt, lt
  Comparator comparator_2 (.a(Opcode), .b(8'h2), .eq(comparator_2_eq));  // open: gt, lt
  Comparator comparator_3 (.a(Opcode), .b(8'h3), .eq(comparator_3_eq));  // open: gt, lt
  Comparator comparator_4 (.a(Opcode), .b(8'h4), .eq(comparator_4_eq));  // open: gt, lt
  or or_1 (Reg_Select, comparator_2_eq, comparator_4_eq);
  or or_2 (ALU_Op, comparator_3_eq, comparator_4_eq);
  or or_3 (Bus_Select[0], comparator_1_eq, comparator_2_eq, comparator_3_eq, comparator_4_eq);

  assign Bus_Select[1] = 1'b0;
  assign Write_Enable = Bus_Select[0];
endmodule

module main (
  input  [7:0] Data_In,
  input  Load_IR,
  input  Load_A,
  input  Load_B,
  output [7:0] IR_Out,
  output [7:0] A_Out,
  output [7:0] B_Out
);

  wire and_1_out, and_2_out, clock_1_out, DECODER_alu_op, DECODER_reg_select, DECODER_write_enable,
       not_1_out, or_1_out, or_2_out;
  wire [1:0] DECODER_bus_select;
  wire [7:0] ALU_result, multiplexer_1_out, multiplexer_2_out, multiplexer_3_out, multiplexer_4_out,
       multiplexer_5_out, multiplexer_6_out, multiplexer_7_out;

  Clock clock_1 (.out(clock_1_out));
  Multiplexer #(.width(8)) multiplexer_1 (
    .in0(multiplexer_7_out), .in1(Data_In), .out(multiplexer_1_out), .sel(Load_IR));  // open: en
  Multiplexer #(.width(8)) multiplexer_2 (
    .in0(A_Out), .in1(multiplexer_3_out), .out(multiplexer_2_out), .sel(or_1_out));  // open: en
  Multiplexer #(.width(8)) multiplexer_3 (
    .in0(multiplexer_7_out), .in1(Data_In), .out(multiplexer_3_out), .sel(Load_A));  // open: en
  Multiplexer #(.width(8)) multiplexer_4 (
    .in0(multiplexer_7_out), .in1(Data_In), .out(multiplexer_4_out), .sel(Load_B));  // open: en
  Multiplexer #(.width(8)) multiplexer_5 (
    .in0(B_Out), .in1(multiplexer_4_out), .out(multiplexer_5_out), .sel(or_2_out));  // open: en
  Register IR (.D(multiplexer_1_out), .en(Load_IR), .Q(IR_Out), .clk(clock_1_out));  // open: clr
  Register A (.D(multiplexer_2_out), .en(or_1_out), .Q(A_Out), .clk(clock_1_out));  // open: clr
  Register B (.D(multiplexer_5_out), .en(or_2_out), .Q(B_Out), .clk(clock_1_out));  // open: clr
  Multiplexer #(.width(8)) multiplexer_6 (
    .in0(A_Out), .in1(B_Out), .out(multiplexer_6_out), .sel(DECODER_reg_select));  // open: en
  Decoder DECODER (
    .Opcode(IR_Out), .Reg_Select(DECODER_reg_select), .ALU_Op(DECODER_alu_op),
    .Write_Enable(DECODER_write_enable), .Bus_Select(DECODER_bus_select));
  or or_1 (or_1_out, Load_A, and_1_out);
  or or_2 (or_2_out, Load_B, and_2_out);
  not not_1 (not_1_out, DECODER_reg_select);
  ALU ALU (.Input_Data(multiplexer_6_out), .Operation(DECODER_alu_op), .Result(ALU_result));
  and and_1 (and_1_out, DECODER_write_enable, not_1_out);
  and and_2 (and_2_out, DECODER_write_enable, DECODER_reg_select);
  Multiplexer #(.select(2), .width(8)) multiplexer_7 (
    .in1(ALU_result), .out(multiplexer_7_out), .sel(DECODER_bus_select));  // open: in0, in2, in3, en

  // Notes on the sheet:
  //                SELECT A
  //          SELECT B
endmodule
