// Logisim project mp.circ as structural Verilog: 3 circuits, main circuit main
module main (
  input  [7:0] Data_In,
  input  LOAD_IR,
  input  [1:0] Bus_Select,
  input  [7:0] Data_In_2,
  input  Load_IR_2,
  input  Load_A,
  output [7:0] IR_Out,
  output [7:0] A_Out,
  output [7:0] B_Out,
  output [7:0] IR_Out_2,
  output [7:0] A_Out_2,
  output [7:0] B_Out_2
);

  wire and_1_out, and_2_out, and_3_out, and_4_out, clock_1_out, clock_2_out, decoder_1_alu_op,
       decoder_1_reg_select, decoder_1_write_enable, decoder_2_alu_op, decoder_2_reg_select,
       decoder_2_write_enable, not_1_out, not_2_out, or_1_out, undriven;
  wire [1:0] decoder_1_bus_select;
  wire [7:0] alu_2_result, multiplexer_1_out, multiplexer_2_out, multiplexer_3_out, multiplexer_4_out,
       multiplexer_5_out, multiplexer_6_out, multiplexer_7_out, multiplexer_8_out;

  Clock clock_1 (.out(clock_1_out));
  Clock clock_2 (.out(clock_2_out));
  Multiplexer #(.select(2), .width(8)) multiplexer_1 (
    .in0(Data_In_2), .in1(alu_2_result), .in3({8{1'b0}}), .out(multiplexer_1_out), .sel(decoder_1_bus_select));  // open: in2, en
  buf or_1 (or_1_out, Load_A);  // OR_Gate
  Multiplexer #(.select(2), .width(8)) multiplexer_2 (
    .in0(Data_In), .in1(Data_In), .in3({8{1'b0}}), .out(multiplexer_2_out), .sel(Bus_Select));  // open: in2, en
  Register IR (.D(multiplexer_1_out), .en(Load_IR_2), .Q(IR_Out_2), .clk(clock_2_out));  // open: clr
  Register IR_2 (.D(multiplexer_2_out), .en(LOAD_IR), .Q(IR_Out), .clk(clock_1_out));  // open: clr
  Multiplexer #(.width(8)) multiplexer_3 (
    .in0(A_Out), .in1(multiplexer_2_out), .out(multiplexer_3_out), .sel(and_3_out));  // open: en
  Decoder decoder_1 (
    .Opcode(IR_Out_2), .Reg_Select(decoder_1_reg_select), .ALU_Op(decoder_1_alu_op),
    .Write_Enable(decoder_1_write_enable), .Bus_Select(decoder_1_bus_select));
  Multiplexer #(.width(8)) multiplexer_4 (
    .in0(A_Out_2), .in1(multiplexer_1_out), .out(multiplexer_4_out), .sel(and_1_out));  // open: en
  Multiplexer #(.width(8)) multiplexer_5 (
    .in0(B_Out_2), .in1(multiplexer_1_out), .out(multiplexer_5_out), .sel(and_2_out));  // open: en
  Decoder decoder_2 (
    .Opcode(IR_Out), .Reg_Select(decoder_2_reg_select), .ALU_Op(decoder_2_alu_op),
    .Write_Enable(decoder_2_write_enable), .Bus_Select(Bus_Select));
  Multiplexer #(.width(8)) multiplexer_6 (
    .in0(B_Out), .in1(multiplexer_2_out), .out(multiplexer_6_out), .sel(and_4_out));  // open: en
  Register A (.D(multiplexer_4_out), .Q(A_Out_2), .clk(clock_2_out), .clr(undriven));  // open: en
  Register B (.D(multiplexer_5_out), .Q(B_Out_2), .clk(clock_2_out));  // open: en, clr
  not not_1 (not_1_out, decoder_2_reg_select);
  Register A_2 (.D(multiplexer_3_out), .Q(A_Out), .clk(clock_1_out));  // open: en, clr
  Register B_2 (.D(multiplexer_6_out), .Q(B_Out), .clk(clock_1_out));  // open: en, clr
  not not_2 (not_2_out, decoder_1_reg_select);
  and and_1 (and_1_out, not_2_out, decoder_1_write_enable);
  and and_2 (and_2_out, decoder_1_write_enable, decoder_1_reg_select);
  and and_3 (and_3_out, decoder_2_write_enable, not_1_out);
  Multiplexer #(.width(8)) multiplexer_7 (
    .in0(A_Out), .in1(B_Out), .out(multiplexer_7_out), .sel(decoder_2_reg_select));  // open: en
  and and_4 (and_4_out, decoder_2_write_enable, decoder_2_reg_select);
  Multiplexer #(.width(8)) multiplexer_8 (
    .in0(A_Out_2), .in1(B_Out_2), .out(multiplexer_8_out), .sel(decoder_1_reg_select));  // open: en
  ALU alu_1 (.Input_Data(multiplexer_7_out), .Operation(decoder_2_alu_op), .Result(Data_In));
  ALU alu_2 (.Input_Data(multiplexer_8_out), .Operation(decoder_1_alu_op), .Result(alu_2_result));
endmodule

module ALU (
  input  [7:0] Input_Data,
  input  Operation,
  output [7:0] Result
);

  Multiplexer #(.width(8)) multiplexer_1 (
    .in0({Input_Data[6:0], Input_Data[7]}), .in1({Input_Data[0], Input_Data[7:1]}), .out(Result),
    .sel(Operation));  // open: en
endmodule

module Decoder (
  input  [7:0] Opcode,
  output Reg_Select,
  output ALU_Op,
  output Write_Enable,
  output [1:0] Bus_Select
);

  wire comparator_1_eq, comparator_2_eq, comparator_3_eq, comparator_4_eq;

  Comparator comparator_1 (.a(Opcode), .b(8'h1), .eq(comparator_1_eq));  // open: gt, lt
  Comparator comparator_2 (.a(Opcode), .b(8'h2), .eq(comparator_2_eq));  // open: gt, lt
  Comparator comparator_3 (.a(Opcode), .b(8'h3), .eq(comparator_3_eq));  // open: gt, lt
  Comparator comparator_4 (.a(Opcode), .b(8'h4), .eq(comparator_4_eq));  // open: gt, lt
  or or_1 (Reg_Select, comparator_2_eq, comparator_4_eq);
  or or_2 (ALU_Op, comparator_3_eq, comparator_4_eq);
  or or_3 (Bus_Select[0], comparator_1_eq, comparator_2_eq, comparator_3_eq, comparator_4_eq);

  assign Bus_Select[1] = 1'b0;
  assign Write_Enable = Bus_Select[0];
endmodule
